// Logisim project project cn262.circ as structural Verilog: 3 circuits, main circuit wall
module wall (
  input  Mode,
  input  Left_right
);

  wire character_1_die_signal, Clock, clock_1_out, clock_2_out, clock_3_out, clock_4_out, clock_5_out,
       clock_6_out, clock_7_out, clock_8_out, comparator_1_eq, comparator_2_eq, comparator_3_eq,
       comparator_4_eq, comparator_5_eq, comparator_6_eq, comparator_7_eq, counter_3_carry, counter_4_carry,
       multiplexer_2_out, nor_1_out, nor_2_out, nor_3_out, nor_4_out, or_1_out, or_2_out, or_3_out, or_4_out,
       or_5_out, random_1_out, reset;
  wire [3:0] counter_2_q, counter_3_q, counter_4_q;
  wire [6:0] keyboard_1_data;
  wire [7:0] counter_1_q, divider_1_rem;
  wire [31:0] character_1_output1, character_1_output2, character_1_output3, character_1_output4,
       character_1_output5, multiplexer_1_out, multiplexer_3_out, slide_1_out_5, slide_1_out_6,
       slide_1_out_7, slide_1_out_8, slide_1_out_9, slide_1_out_10, slide_1_out_11, slide_1_out_12,
       slide_1_out_13, slide_1_out_14, slide_1_out_15, slide_1_out_16, slide_1_out_17, slide_1_out_18,
       slide_1_out_19, slide_1_out_20, slide_1_out_21, slide_1_out_22, slide_1_out_23, slide_1_out_24,
       slide_1_out_25, slide_1_out_26, slide_1_out_27, slide_1_out_28, slide_1_out_29, slide_1_out_30,
       slide_1_out_31, slide_1_out_32, slide_1_out_33, slide_1_out_34, slide_1_out_35, slide_1_out_36;

  nor nor_1 (nor_1_out, nor_2_out, character_1_die_signal);
  Button button_1 (.out(reset));
  nor nor_2 (nor_2_out, nor_1_out, reset);
  Random #(.width(1)) random_1 (.clk(Clock), .out(random_1_out));  // open: next, clr
  Counter counter_1 (.Q(counter_1_q), .clk(Clock));  // open: load, D, count, carry, clr
  Multiplexer #(.width(32)) multiplexer_1 (
    .in0(32'hfff00001), .in1(32'h80000fff), .out(multiplexer_1_out), .sel(random_1_out));  // open: en
  Divider divider_1 (.a(counter_1_q), .b(8'h10), .rem(divider_1_rem));  // open: out, upper
  Multiplexer multiplexer_2 (.in0(Left_right), .in1(nor_3_out), .out(multiplexer_2_out), .sel(Mode));  // open: en
  Comparator comparator_1 (.a(divider_1_rem), .b({8{1'b0}}), .eq(comparator_1_eq));  // open: gt, lt
  nor nor_3 (nor_3_out, or_1_out, nor_4_out);
  nor nor_4 (nor_4_out, nor_3_out, or_2_out);
  Multiplexer #(.width(32)) multiplexer_3 (
    .in0(32'h80000001), .in1(multiplexer_1_out), .out(multiplexer_3_out), .sel(comparator_1_eq));  // open: en
  character character_1 (
    .in1(slide_1_out_29), .in2(slide_1_out_30), .in3(slide_1_out_31), .in4(slide_1_out_32),
    .in5(slide_1_out_33), .Position(multiplexer_2_out), .Reset(reset), .Die_signal(character_1_die_signal),
    .output1(character_1_output1), .output2(character_1_output2), .output3(character_1_output3),
    .output4(character_1_output4), .output5(character_1_output5), .Clock(Clock));
  slide slide_1 (
    .in_3(multiplexer_3_out), .out_30(slide_1_out_30), .out_31(slide_1_out_31), .out_32(slide_1_out_32),
    .out_33(slide_1_out_33), .out_5(slide_1_out_5), .out_6(slide_1_out_6), .out_7(slide_1_out_7),
    .out_8(slide_1_out_8), .out_9(slide_1_out_9), .out_10(slide_1_out_10), .out_11(slide_1_out_11),
    .out_12(slide_1_out_12), .out_13(slide_1_out_13), .out_14(slide_1_out_14), .out_15(slide_1_out_15),
    .out_16(slide_1_out_16), .out_17(slide_1_out_17), .out_18(slide_1_out_18), .out_19(slide_1_out_19),
    .out_20(slide_1_out_20), .out_21(slide_1_out_21), .out_22(slide_1_out_22), .out_23(slide_1_out_23),
    .out_24(slide_1_out_24), .out_25(slide_1_out_25), .out_26(slide_1_out_26), .out_27(slide_1_out_27),
    .out_28(slide_1_out_28), .out_34(slide_1_out_34), .out_35(slide_1_out_35), .out_29(slide_1_out_29),
    .out_36(slide_1_out_36), .Die(nor_2_out), .Reset(reset), .Clock(Clock));
  Keyboard keyboard_1 (.clk(Clock), .data(keyboard_1_data));  // open: re, clr, avail
  or or_1 (or_1_out, comparator_2_eq, comparator_3_eq);
  or or_2 (or_2_out, comparator_4_eq, comparator_5_eq);
  DotMatrix #(.inputtype("row"), .matrixcols(32), .matrixrows(32)) dotmatrix_1 (
    .row0(slide_1_out_5), .row1(slide_1_out_6), .row2(slide_1_out_7), .row3(slide_1_out_8),
    .row4(slide_1_out_9), .row5(slide_1_out_10), .row6(slide_1_out_11), .row7(slide_1_out_12),
    .row8(slide_1_out_13), .row9(slide_1_out_14), .row10(slide_1_out_15), .row11(slide_1_out_16),
    .row12(slide_1_out_17), .row13(slide_1_out_18), .row14(slide_1_out_19), .row15(slide_1_out_20),
    .row16(slide_1_out_21), .row17(slide_1_out_22), .row18(slide_1_out_23), .row19(slide_1_out_24),
    .row20(slide_1_out_25), .row21(slide_1_out_26), .row22(slide_1_out_27), .row23(slide_1_out_28),
    .row24(character_1_output1), .row25(character_1_output2), .row26(character_1_output3),
    .row27(character_1_output4), .row28(character_1_output5), .row29(slide_1_out_34), .row30(slide_1_out_35),
    .row31(slide_1_out_36));
  Comparator #(.width(7), .mode("unsigned")) comparator_2 (
    .a(keyboard_1_data), .b(7'b1000001), .eq(comparator_2_eq));  // open: gt, lt
  Comparator #(.width(7), .mode("unsigned")) comparator_3 (
    .a(keyboard_1_data), .b(7'b1100001), .eq(comparator_3_eq));  // open: gt, lt
  Comparator #(.width(7), .mode("unsigned")) comparator_4 (
    .a(keyboard_1_data), .b(7'b1000100), .eq(comparator_4_eq));  // open: gt, lt
  Comparator #(.width(7), .mode("unsigned")) comparator_5 (
    .a(keyboard_1_data), .b(7'b1100100), .eq(comparator_5_eq));  // open: gt, lt
  Comparator #(.width(32)) comparator_6 (.a(32'hfff00001), .b(slide_1_out_36), .eq(comparator_6_eq));  // open: gt, lt
  Comparator #(.width(32)) comparator_7 (.a(slide_1_out_36), .b(32'h80000fff), .eq(comparator_7_eq));  // open: gt, lt
  Counter #(.width(4), .max('h9)) counter_2 (
    .Q(counter_2_q), .clk(counter_3_carry), .clr(reset));  // open: load, D, count, carry
  or or_3 (or_3_out, comparator_6_eq, comparator_7_eq);
  Hex_Digit_Display hex_digit_display_1 (.value(counter_3_q));  // open: dp
  Hex_Digit_Display hex_digit_display_2 (.value(counter_2_q));  // open: dp
  Counter #(.width(4), .max('ha)) counter_3 (
    .Q(counter_3_q), .carry(counter_3_carry), .clk(counter_4_carry), .clr(or_4_out));  // open: load, D, count
  or or_4 (or_4_out, counter_3_carry, reset);
  Hex_Digit_Display hex_digit_display_3 (.value(counter_4_q));  // open: dp
  Counter #(.width(4), .max('ha)) counter_4 (
    .Q(counter_4_q), .carry(counter_4_carry), .clk(or_3_out), .clr(or_5_out));  // open: load, D, count
  or or_5 (or_5_out, counter_4_carry, reset);
  Clock #(.highDuration(8), .lowDuration(8)) clock_1 (.out(clock_1_out));
  Clock #(.highDuration(7), .lowDuration(7)) clock_2 (.out(clock_2_out));
  Clock #(.highDuration(6), .lowDuration(6)) clock_3 (.out(clock_3_out));
  Clock #(.highDuration(5), .lowDuration(5)) clock_4 (.out(clock_4_out));
  Clock #(.highDuration(4), .lowDuration(4)) clock_5 (.out(clock_5_out));
  Clock #(.highDuration(3), .lowDuration(3)) clock_6 (.out(clock_6_out));
  Clock #(.highDuration(2), .lowDuration(2)) clock_7 (.out(clock_7_out));
  Clock clock_8 (.out(clock_8_out));
  Multiplexer #(.select(4)) multiplexer_4 (
    .in0(clock_1_out), .in1(clock_2_out), .in2(clock_3_out), .in3(clock_4_out), .in4(clock_5_out),
    .in5(clock_6_out), .in6(clock_7_out), .in7(clock_8_out), .in8(clock_8_out), .out(Clock), .sel(counter_3_q));  // open: in9, in10, in11, in12, in13, in14, in15, en

  // Notes on the sheet:
  //   0: click Mode
  //   1: key board Mode
endmodule

module slide (
  input  Clock,
  input  Die,
  input  [31:0] in_3,
  input  Reset,
  output [31:0] out_5,
  output [31:0] out_6,
  output [31:0] out_7,
  output [31:0] out_8,
  output [31:0] out_9,
  output [31:0] out_10,
  output [31:0] out_11,
  output [31:0] out_12,
  output [31:0] out_13,
  output [31:0] out_14,
  output [31:0] out_15,
  output [31:0] out_16,
  output [31:0] out_17,
  output [31:0] out_18,
  output [31:0] out_19,
  output [31:0] out_20,
  output [31:0] out_21,
  output [31:0] out_22,
  output [31:0] out_23,
  output [31:0] out_24,
  output [31:0] out_25,
  output [31:0] out_26,
  output [31:0] out_27,
  output [31:0] out_28,
  output [31:0] out_29,
  output [31:0] out_30,
  output [31:0] out_31,
  output [31:0] out_32,
  output [31:0] out_33,
  output [31:0] out_34,
  output [31:0] out_35,
  output [31:0] out_36
);

  wire tick;
  wire [31:0] register_29_q;

  Register #(.width(32)) register_1 (.D(in_3), .Q(out_5), .clk(tick), .clr(Reset));  // open: en
  Register #(.width(32)) register_2 (.D(out_5), .Q(out_6), .clk(tick), .clr(Reset));  // open: en
  Register #(.width(32)) register_3 (.D(out_6), .Q(out_7), .clk(tick), .clr(Reset));  // open: en
  Register #(.width(32)) register_4 (.D(out_7), .Q(out_8), .clk(tick), .clr(Reset));  // open: en
  Register #(.width(32)) register_5 (.D(out_8), .Q(out_9), .clk(tick), .clr(Reset));  // open: en
  Register #(.width(32)) register_6 (.D(out_9), .Q(out_10), .clk(tick), .clr(Reset));  // open: en
  Register #(.width(32)) register_7 (.D(out_10), .Q(out_11), .clk(tick), .clr(Reset));  // open: en
  Transistor transistor_1 (.in(Clock), .out(tick), .gate(Die));
  Register #(.width(32)) register_8 (.D(out_11), .Q(out_12), .clk(tick), .clr(Reset));  // open: en
  Register #(.width(32)) register_9 (.D(out_12), .Q(out_13), .clk(tick), .clr(Reset));  // open: en
  Register #(.width(32)) register_10 (.D(out_13), .Q(out_14), .clk(tick), .clr(Reset));  // open: en
  Register #(.width(32)) register_11 (.D(out_14), .Q(out_15), .clk(tick), .clr(Reset));  // open: en
  Register #(.width(32)) register_12 (.D(out_15), .Q(out_16), .clk(tick), .clr(Reset));  // open: en
  Register #(.width(32)) register_13 (.D(out_16), .Q(out_17), .clk(tick), .clr(Reset));  // open: en
  Register #(.width(32)) register_14 (.D(out_17), .Q(out_18), .clk(tick), .clr(Reset));  // open: en
  Register #(.width(32)) register_15 (.D(out_18), .Q(out_19), .clk(tick), .clr(Reset));  // open: en
  Register #(.width(32)) register_16 (.D(out_19), .Q(out_20), .clk(tick), .clr(Reset));  // open: en
  Register #(.width(32)) register_17 (.D(out_20), .Q(out_21), .clk(tick), .clr(Reset));  // open: en
  Register #(.width(32)) register_18 (.D(out_21), .Q(out_22), .clk(tick), .clr(Reset));  // open: en
  Register #(.width(32)) register_19 (.D(out_22), .Q(out_23), .clk(tick), .clr(Reset));  // open: en
  Register #(.width(32)) register_20 (.D(out_23), .Q(out_24), .clk(tick), .clr(Reset));  // open: en
  Register #(.width(32)) register_21 (.D(out_24), .Q(out_25), .clk(tick), .clr(Reset));  // open: en
  Register #(.width(32)) register_22 (.D(out_25), .Q(out_26), .clk(tick), .clr(Reset));  // open: en
  Register #(.width(32)) register_23 (.D(out_26), .Q(out_27), .clk(tick), .clr(Reset));  // open: en
  Register #(.width(32)) register_24 (.D(out_27), .Q(out_28), .clk(tick), .clr(Reset));  // open: en
  Register #(.width(32)) register_25 (.D(out_28), .Q(out_30), .clk(tick), .clr(Reset));  // open: en
  Register #(.width(32)) register_26 (.D(out_30), .Q(out_31), .clk(tick), .clr(Reset));  // open: en
  Register #(.width(32)) register_27 (.D(out_31), .Q(out_32), .clk(tick), .clr(Reset));  // open: en
  Register #(.width(32)) register_28 (.D(out_32), .Q(out_33), .clk(tick), .clr(Reset));  // open: en
  Register #(.width(32)) register_29 (.D(out_33), .Q(register_29_q), .clk(tick), .clr(Reset));  // open: en
  Register #(.width(32)) register_30 (.D(register_29_q), .Q(out_34), .clk(tick), .clr(Reset));  // open: en
  Register #(.width(32)) register_31 (.D(out_34), .Q(out_35), .clk(tick), .clr(Reset));  // open: en
  Register #(.width(32)) register_32 (.D(out_35), .Q(out_36), .clk(tick), .clr(Reset));  // open: en

  assign out_29 = out_28;
endmodule

module character (
  input  Reset,
  input  [31:0] in1,
  input  Position,
  input  Clock,
  input  [31:0] in2,
  input  [31:0] in3,
  input  [31:0] in4,
  input  [31:0] in5,
  output [31:0] output1,
  output Die_signal,
  output [31:0] output2,
  output [31:0] output3,
  output [31:0] output4,
  output [31:0] output5
);

  wire _1, _2, _3, _4, _5, _6, _7, _8, _9, _10, or_1_out, or_2_out;
  wire [24:0] register_1_q_2, register_2_q_2, register_3_q_2, register_4_q_2, register_5_q_2;
  wire [25:25] register_4_q_3;
  wire [27:25] register_1_q;
  wire [28:24] register_3_q;
  wire [29:23] register_2_q, register_4_q, register_5_q;
  wire [30:28] register_2_q_3;
  wire [30:29] register_3_q_3;
  wire [31:28] register_1_q_3;

  Register #(.width(32)) register_1 (
    .D(in1),
    .Q({register_1_q_3[31], _2, register_1_q_3[29:28], register_1_q, register_1_q_2[24:2], _1, register_1_q_2[0]}),
    .clk(Clock), .clr(Reset));  // open: en
  Register #(.width(32)) register_2 (
    .D(in5),
    .Q({register_2_q_2[24], register_2_q_3[30], register_2_q[29], register_2_q_3[28], register_2_q[27], _10, register_2_q[25], register_2_q_2[23], register_2_q[23], register_2_q_2[22:6], _9, register_2_q_2[4:0]}),
    .clk(Clock), .clr(Reset));  // open: en
  Register #(.width(32)) register_3 (
    .D(in2),
    .Q({register_3_q_2[24], register_3_q_3, register_3_q[28:26], _4, register_3_q[24], register_3_q_2[23:2], _3, register_3_q_2[0]}),
    .clk(Clock), .clr(Reset));  // open: en
  Register #(.width(32)) register_4 (
    .D(in3),
    .Q({register_4_q_2[24:23], register_4_q[29:28], _6, register_4_q[26], register_4_q_3[25], register_4_q[24:23], register_4_q_2[22:5], _5, register_4_q_2[3:0]}),
    .clk(Clock), .clr(Reset));  // open: en
  Register #(.width(32)) register_5 (
    .D(in4),
    .Q({register_5_q_2[24:23], register_5_q[29:28], _8, register_5_q[26:23], register_5_q_2[22:5], _7, register_5_q_2[3:0]}),
    .clk(Clock), .clr(Reset));  // open: en
  Multiplexer #(.width(32)) multiplexer_1 (
    .in0({register_1_q_3[31], _2, register_1_q_3[29:28], 3'b111, register_1_q_2[24:2], _1, register_1_q_2[0]}),
    .in1({register_1_q_3[31], _2, register_1_q_3[29:28], register_1_q, register_1_q_2[24:7], 3'b111, register_1_q_2[3:2], _1, register_1_q_2[0]}),
    .out(output1), .sel(Position));  // open: en
  Multiplexer #(.width(32)) multiplexer_2 (
    .in0({register_3_q_2[24], register_3_q_3, {5{1'b1}}, register_3_q_2[23:2], _3, register_3_q_2[0]}),
    .in1({register_3_q_2[24], register_3_q_3, register_3_q[28:26], _4, register_3_q[24], register_3_q_2[23:8], {5{1'b1}}, register_3_q_2[2], _3, register_3_q_2[0]}),
    .out(output2), .sel(Position));  // open: en
  Multiplexer #(.width(32)) multiplexer_3 (
    .in0({register_4_q_2[24:23], 2'b11, _6, 1'b1, register_4_q_3[25], 2'b11, register_4_q_2[22:5], _5, register_4_q_2[3:0]}),
    .in1({register_4_q_2[24:23], register_4_q[29:28], _6, register_4_q[26], register_4_q_3[25], register_4_q[24:23], register_4_q_2[22:9], 2'b11, register_4_q_2[6], 1'b1, _5, 2'b11, register_4_q_2[1:0]}),
    .out(output3), .sel(Position));  // open: en
  Multiplexer #(.width(32)) multiplexer_4 (
    .in0({register_5_q_2[24:23], {7{1'b1}}, register_5_q_2[22:5], _7, register_5_q_2[3:0]}),
    .in1({register_5_q_2[24:23], register_5_q[29:28], _8, register_5_q[26:23], register_5_q_2[22:9], {7{1'b1}}, register_5_q_2[1:0]}),
    .out(output4), .sel(Position));  // open: en
  Multiplexer #(.width(32)) multiplexer_5 (
    .in0({register_2_q_2[24], register_2_q_3[30], 1'b1, register_2_q_3[28], 1'b1, _10, 1'b1, register_2_q_2[23], 1'b1, register_2_q_2[22:6], _9, register_2_q_2[4:0]}),
    .in1({register_2_q_2[24], register_2_q_3[30], register_2_q[29], register_2_q_3[28], register_2_q[27], _10, register_2_q[25], register_2_q_2[23], register_2_q[23], register_2_q_2[22:9], 1'b1, register_2_q_2[7], 1'b1, _9, 1'b1, register_2_q_2[3], 1'b1, register_2_q_2[1:0]}),
    .out(output5), .sel(Position));  // open: en
  or or_1 (or_1_out, _1, _3, _5, _7, _9);
  Multiplexer multiplexer_6 (.in0(or_2_out), .in1(or_1_out), .out(Die_signal), .sel(Position));  // open: en
  or or_2 (or_2_out, _2, _4, _6, _8, _10);

  // Other names for the same wires on the sheet: tick = Clock

  // Notes on the sheet:
  //   jump right
  //   jump left
endmodule
